# Fritzing sketch ArduinoRobot (saved by Fritzing 0.9.3b)
circuit board: 8.46667cm x 5.64444cm
breadboards: 1

parts:
  Part1 = Arduino Uno (Rev3)
  M2 = DC Motor
  BAT1 = Battery Holders [package=battery-aa]
  BAT2 = Battery Holders [package=battery-aa]
  BAT3 = Battery Holders [package=battery-aa]
  BAT4 = Battery Holders [package=battery-aa]
  S1 = H-Bridge with L298N
  BT1 = Bluetooth HC-06u [package=THT]
  S2 = Pololu QTR-8 Reflectabce Sensor array [package=THT]
  M3 = DC Motor

nets:
  N1: Part1.D8, S1.IN2
  N2: Part1.D9_PWM, S1.IN1
  N3: Part1.D10_PWM/SS, S1.ENA
  N4: Part1.D11_PWM/MOSI, S2.pin9
  N5: Part1.D12/MISO, S2.pin11
  N6: Part1.D13/SCK, S2.pin10
  GND: Part1.GND, BT1.GND, S2.pin15, S2.pin21
  N7: Part1.D0/RX, BT1.TXD
  N8: Part1.D1/TX, BT1.RXD
  N9: Part1.D3_PWM, S2.pin12
  N10: Part1.D4, S2.pin8
  N11: Part1.D5_PWM, S1.ENB
  N12: Part1.D6_PWM, S1.IN4
  N13: Part1.D7, S1.IN3
  3V3: Part1.3V3, BT1.VCC
  5V: Part1.5V, S1.5V, S2.pin2, S2.pin22
  N14: M2.pin_1, S1.M2-02, S1.ENB-5V
  N15: M2.pin_2, S1.M2-01
  N16: BAT1.-, BAT3.+
  N17: BAT1.+, BAT4.-
  N18: BAT2.-, S1.GND
  N19: BAT2.+, BAT3.-
  N20: BAT4.+, S1.12V
  N21: S1.M1-01, M3.pin_2
  N22: S1.M1-02, M3.pin_1

custom parts:
  H-Bridge with L298N: h-bridge
  Bluetooth HC-06u: Bluetooth HC-06 - face up, pins down 16.5mm x 37.5mm PCB

// code stored in the sketch: BluetoothRC.ino
char incomingByte; // variable to receive data from the serial port
int speedValue=120;

// MOTOR PIN ASSIGNMENTS
// Left motor
int enA = 10;  //Remove jumper and plug to outer pin of ENA
int in1 = 9;
int in2 = 8;

// Right motor
int in3 = 7;
int in4 = 6;
int enB = 5;  //Remove jumper and plug to outer pin of ENB


void setup()
{
  Serial.begin(9600); // start serial communication at 9600 bps
  
  // Make motor as output
  pinMode(enA,OUTPUT);
  pinMode(in1,OUTPUT);
  pinMode(in2,OUTPUT);
  pinMode(in3,OUTPUT);
  pinMode(in4,OUTPUT);
  pinMode(enB,OUTPUT);

}

void loop()
{
  if(Serial.available()>0)  // if data is available to read
  {
    incomingByte = Serial.read(); //read it and store it in 'incomingByte'
    
    
    // Move according to BT status

    switch (incomingByte)
    {
      case 'W':
        moveForward();
        Serial.println(incomingByte);
        break;
      case 'D':
        moveRight();
        Serial.println(incomingByte);
        break;
      case 'A':
        moveLeft();
        Serial.println(incomingByte);
        break;
      case 'S':
        moveBack();
        Serial.println(incomingByte);
        break;
     
        
/*
  if (incomingByte=='W')
    moveForward();
    Serial.println(incomingByte);
  if (incomingByte=='D')
    moveRight();
    Serial.println(incomingByte);
  if (incomingByte=='A')
    moveLeft();
    Serial.println(incomingByte);
  if (incomingByte=='S')
    moveBack();
    Serial.println(incomingByte);
*/
    }
  }
}

void moveForward(void)
{
  digitalWrite(in3,HIGH);
  digitalWrite(in4,LOW);
  analogWrite(enB,speedValue);
  digitalWrite(in2,HIGH);
  digitalWrite(in1,LOW);
  analogWrite(enA,speedValue);
}

void moveRight(void)
{
  digitalWrite(in3,HIGH);
  digitalWrite(in4,LOW);
  analogWrite(enB,0);
  digitalWrite(in2,HIGH);
  digitalWrite(in1,LOW);
  analogWrite(enA,speedValue);
}

void moveLeft(void)
{
  digitalWrite(in3,HIGH);
  digitalWrite(in4,LOW);
  analogWrite(enB,speedValue);
  digitalWrite(in2,HIGH);
  digitalWrite(in1,LOW);
  analogWrite(enA,0);
}

void sharpRight(void)
{
  digitalWrite(in3,LOW);
  digitalWrite(in4,HIGH);
  analogWrite(enB,speedValue);
  digitalWrite(in2,HIGH);
  digitalWrite(in1,LOW);
  analogWrite(enA,speedValue);
}

void sharpLeft(void)
{
  digitalWrite(in3,HIGH);
  digitalWrite(in4,LOW);
  analogWrite(enB,speedValue);
  digitalWrite(in2,LOW);
  digitalWrite(in1,HIGH);
  analogWrite(enA,speedValue);
}


void moveBack(void)
{
  digitalWrite(in3,LOW);
  digitalWrite(in4,HIGH);
  analogWrite(enB,speedValue);
  digitalWrite(in2,LOW);
  digitalWrite(in1,HIGH);
  analogWrite(enA,speedValue);
}

void moveStop(void)
{
  digitalWrite(in1,LOW);
  digitalWrite(in2,LOW);
  digitalWrite(in3,LOW);
  digitalWrite(in4,LOW);
}

// code stored in the sketch: SimpleLineFollower.ino
/*
Simple line follower program using:
- Arduino Uno
- L298N motor driver
- 2 DC motors
- 5 x IR sensor
Created by Asep Nurul Haq.
*/

// MOTOR PIN ASSIGNMENTS
// Left motor
int enA = 10;  //Remove jumper and plug to outer pin of ENA
int in1 = 9;
int in2 = 8;

// Right motor
int in3 = 7;
int in4 = 6;
int enB = 5;  //Remove jumper and plug to outer pin of ENB

// IR PIN ASSIGNMENTS
int MiddleIRPin = 13;
int RightIRPin = 11;
int LeftIRPin = 12;
int RRIRPin = 4; //Most right IR
int LLIRPin =3; // Most left IR
int MiddleIR;
int RightIR;
int LeftIR;
int RRIR;
int LLIR;

// SET VARIABLES
int speedValue = 120;
int halfSpeed = speedValue/2;
int delayValue = 3000;

void setup()
{
  // Make IR as input
  pinMode(RRIRPin, INPUT);
  pinMode(LLIRPin, INPUT);
  pinMode(MiddleIRPin, INPUT);
  pinMode(RightIRPin, INPUT);
  pinMode(LeftIRPin, INPUT);
  // Make motor as output
  pinMode(enA,OUTPUT);
  pinMode(in1,OUTPUT);
  pinMode(in2,OUTPUT);
  pinMode(in3,OUTPUT);
  pinMode(in4,OUTPUT);
  pinMode(enB,OUTPUT);
}


void loop() 
{
  
// Read value of IR    
RRIR=digitalRead(RRIRPin);
LLIR=digitalRead(LLIRPin);
MiddleIR=digitalRead(MiddleIRPin);
RightIR=digitalRead(RightIRPin);
LeftIR=digitalRead(LeftIRPin);

// Move according to IR status
  if (RRIR==0)
    sharpRight();
  else if (LLIR==0)
    sharpLeft();
  else if ((RightIR==0 && LeftIR ==1)==1)
    moveRight();
  else if ((LeftIR==0 && RightIR==1)==1)
    moveLeft();
  else if ((MiddleIR==0 && LeftIR==1 && RightIR == 1)==1)
    moveForward();
}

void moveForward(void)
{
  digitalWrite(in3,HIGH);
  digitalWrite(in4,LOW);
  analogWrite(enB,speedValue);
  digitalWrite(in2,HIGH);
  digitalWrite(in1,LOW);
  analogWrite(enA,speedValue);
}

void moveRight(void)
{
  digitalWrite(in3,HIGH);
  digitalWrite(in4,LOW);
  analogWrite(enB,0);
  digitalWrite(in2,HIGH);
  digitalWrite(in1,LOW);
  analogWrite(enA,speedValue);
}

void moveLeft(void)
{
  digitalWrite(in3,HIGH);
  digitalWrite(in4,LOW);
  analogWrite(enB,speedValue);
  digitalWrite(in2,HIGH);
  digitalWrite(in1,LOW);
  analogWrite(enA,0);
}

void sharpRight(void)
{
  digitalWrite(in3,LOW);
  digitalWrite(in4,HIGH);
  analogWrite(enB,speedValue);
  digitalWrite(in2,HIGH);
  digitalWrite(in1,LOW);
  analogWrite(enA,speedValue);
}

void sharpLeft(void)
{
  digitalWrite(in3,HIGH);
  digitalWrite(in4,LOW);
  analogWrite(enB,speedValue);
  digitalWrite(in2,LOW);
  digitalWrite(in1,HIGH);
  analogWrite(enA,speedValue);
}
